// Logisim project Real_Alu-Gabri-salvo.circ as structural Verilog
module A_And_B (
  input  [7:0] A,
  input  [7:0] B,
  output [7:0] out_3
);

  assign out_3 = A & B;  // AND_Gate and_1, 8 bits wide
endmodule

module NOT_in_B (
  input  [7:0] B,
  output [7:0] NOT_B
);

  assign NOT_B = ~B;  // NOT_Gate not_1, 8 bits wide
endmodule
